// Logisim project guia_2.circ as structural Verilog
module demultiplexor (
  input  c1,
  input  c0,
  input  e0,
  output s0,
  output s1,
  output s2,
  output s3
);

  and and_1 (s0, ~c1, e0, ~c0);  // AND_Gate
  and and_2 (s1, ~c1, e0, c0);  // AND_Gate
  and and_3 (s2, c1, e0, ~c0);  // AND_Gate
  and and_4 (s3, c1, e0, c0);
endmodule

module inversor (
  input  e2,
  input  e1,
  input  e0,
  input  c0,
  output s2,
  output s1,
  output s0
);

  xor xor_1 (s2, c0, e2);
  xor xor_2 (s1, c0, e1);
  xor xor_3 (s0, c0, e0);
endmodule

module inversoAditivo (
  input  [3:0] e,
  output [3:0] s,
  output nr
);

  wire [3:0] not_1_out;

  assign not_1_out = ~e;  // NOT_Gate not_1, 4 bits wide
  and and_1 (nr, ~e[0], ~e[1], ~e[2], e[3]);  // AND_Gate
  sumBin4b sumbin4b_1 (.e0(not_1_out), .e1(4'b0001), .s(s));  // open: c
endmodule

module sumBin4b (
  input  [3:0] e0,
  input  [3:0] e1,
  output c,
  output [3:0] s
);

  wire sumbin1b_2_co, sumbin1b_3_co, sumbin1b_4_co;

  sumBin1b sumbin1b_1 (.cO(c), .e1(e1[3]), .e0(e0[3]), .res(s[3]), .cI(sumbin1b_2_co));
  sumBin1b sumbin1b_2 (.cO(sumbin1b_2_co), .e1(e1[2]), .e0(e0[2]), .res(s[2]), .cI(sumbin1b_3_co));
  sumBin1b sumbin1b_3 (.cO(sumbin1b_3_co), .e1(e1[1]), .e0(e0[1]), .res(s[1]), .cI(sumbin1b_4_co));
  sumBin1b sumbin1b_4 (.cO(sumbin1b_4_co), .e1(e1[0]), .e0(e0[0]), .res(s[0]), .cI(1'b0));
endmodule

module sumBin1b (
  input  e1,
  input  e0,
  input  cI,
  output cO,
  output res
);

  wire and_1_out, and_2_out, xor_1_out;

  or or_1 (cO, and_1_out, and_2_out);
  and and_1 (and_1_out, e0, e1);
  and and_2 (and_2_out, cI, xor_1_out);
  xor xor_1 (xor_1_out, e1, e0);
  xor xor_2 (res, xor_1_out, cI);
endmodule

module codificador (
  input  [3:0] e,
  output [1:0] s,
  output v
);

  or or_1 (s[0], e[1], e[3]);
  or or_2 (s[1], e[2], e[3]);
  ExactlyOne xor_1 (.out(v), .in0(e[0]), .in1(e[1]), .in2(e[2]), .in3(e[3]));
endmodule

module decodificador (
  input  [1:0] e,
  output [3:0] s
);

  and and_1 (s[0], ~e[0], ~e[1]);  // AND_Gate
  and and_2 (s[1], e[0], ~e[1]);  // AND_Gate
  and and_3 (s[2], ~e[0], e[1]);  // AND_Gate
  and and_4 (s[3], e[0], e[1]);
endmodule

module demultiplex (
  input  e,
  input  c0,
  input  c1,
  output s0,
  output s1,
  output s2,
  output s3
);

  wire [3:0] decodificador_1_s;

  decodificador decodificador_1 (.e({c1, c0}), .s(decodificador_1_s));
  and and_1 (s0, e, decodificador_1_s[0]);
  and and_2 (s1, e, decodificador_1_s[1]);
  and and_3 (s2, e, decodificador_1_s[2]);
  and and_4 (s3, e, decodificador_1_s[3]);
endmodule

module ej12 (
  input  x,
  output A,
  output B
);

  wire and_1_out, clock_1_out, d_ff_1_qn, nor_1_out;

  nor nor_1 (nor_1_out, A, x);
  and and_1 (and_1_out, A, d_ff_1_qn);
  Clock clock_1 (.out(clock_1_out));
  J_K_Flip_Flop j_k_ff_1 (.J(nor_1_out), .K(nor_1_out), .clk(clock_1_out), .Q(A));  // open: Qn, preset, reset
  D_Flip_Flop d_ff_1 (.D(and_1_out), .clk(clock_1_out), .Q(B), .Qn(d_ff_1_qn));  // open: preset, reset
endmodule
